# Fritzing sketch neelbsketch  (saved by Fritzing 0.9.2b)
breadboards: 1

parts:
  LED1 = LED - 5mm [color="Red (633nm)" package="5 mm [THT]"]
  LED2 = LED - 5mm [color="Red (633nm)" package="5 mm [THT]"]
  LED3 = LED - 5mm [color="Red (633nm)" package="5 mm [THT]"]
  LED4 = LED - 5mm [color="Green (555nm)" package="5 mm [THT]"]
  LED5 = LED - 5mm [color="Green (555nm)" package="5 mm [THT]"]
  LED6 = LED - 5mm [color="Green (555nm)" package="5 mm [THT]"]
  LED7 = LED - 5mm [color="Green (555nm)" package="5 mm [THT]"]
  Power_plug1 = Power plug
  C1 = Electrolytic Capacitor [capacitance=1µF package="100 mil [THT, electrolytic]"]
  C2 = Electrolytic Capacitor [capacitance=1µF package="100 mil [THT, electrolytic]"]
  C3 = Electrolytic Capacitor [capacitance=1µF package="100 mil [THT, electrolytic]"]
  R1 = Resistor [tolerance=±5% resistance=220 package=THT]
  Q1 = NPN-Transistor [package="TO92 [THT]"]
  R2 = Resistor [tolerance=±5% resistance=220 package=THT]
  R3 = Resistor [tolerance=±5% resistance=220 package=THT]
  Q2 = NPN-Transistor [package="TO92 [THT]"]
  R4 = Resistor [tolerance=±5% resistance=220 package=THT]

nets:
  N1: LED1.cathode, LED2.cathode, LED3.cathode, C1.-, R3.Pin_1
  N2: LED1.anode, LED2.anode, LED3.anode, LED4.anode, LED5.anode, LED6.anode, LED7.anode, Power_plug1.VCC, C1.+, R1.Pin_1, R2.Pin_1
  N3: LED4.cathode, LED5.cathode, LED6.cathode, LED7.cathode, R4.Pin_1
  N4: Power_plug1.GND, Q1.E, Q2.C
  N5: C2.-, Q1.B, R2.Pin_0
  N6: C2.+, R3.Pin_0, Q2.E
  N7: C3.-, R1.Pin_0
  N8: C3.+, Q1.C, R4.Pin_0
